// Logisim project homework.circ as structural Verilog: 3 circuits, main circuit main
module main (
);

  wire clock_1_out, Counter_q0, Counter_q1, Counter_q2, Counter_q3, Driver_a_2, Driver_b_2, Driver_c_2,
       Driver_d_2, Driver_e, Driver_f, Driver_g;

  Clock clock_1 (.out(clock_1_out));
  counter Counter (.CLK(clock_1_out), .Q3(Counter_q3), .Q2(Counter_q2), .Q1(Counter_q1), .Q0(Counter_q0));
  driver Driver (
    .A(Counter_q3), .B(Counter_q2), .C(Counter_q1), .D(Counter_q0), .a_2(Driver_a_2), .b_2(Driver_b_2),
    .c_2(Driver_c_2), .d_2(Driver_d_2), .e(Driver_e), .f(Driver_f), .g(Driver_g));
  _7_Segment_Display u_7_segment_display_1 (
    .g(Driver_g), .f(Driver_f), .a(Driver_a_2), .b(Driver_b_2), .e(Driver_e), .d(Driver_d_2), .c(Driver_c_2));  // open: dp

  // Notes on the sheet:
  //   الاسم الثلاثي هنا
  //   b
  //   a
  //   f
  //   g
  //   e
  //   d
  //   c
endmodule

module driver (
  input  A,
  input  B,
  input  C,
  input  D,
  output a_2,
  output b_2,
  output c_2,
  output d_2,
  output e,
  output f,
  output g
);


  // Notes on the sheet:
  //   قم بإكمال الدارة هنا
endmodule

module counter (
  input  CLK,
  output Q3,
  output Q2,
  output Q1,
  output Q0
);

  J_K_Flip_Flop j_k_ff_1 (.clk(CLK), .Q(Q3));  // open: J, K, Qn, preset, en, reset
  J_K_Flip_Flop j_k_ff_2 (.clk(CLK), .Q(Q2));  // open: J, K, Qn, preset, en, reset
  J_K_Flip_Flop j_k_ff_3 (.clk(CLK), .Q(Q1));  // open: J, K, Qn, preset, en, reset
  J_K_Flip_Flop j_k_ff_4 (.clk(CLK), .Q(Q0));  // open: J, K, Qn, preset, en, reset

  // Notes on the sheet:
  //   قم بتصميم الدارات التركيبية المطبقة على المداخل jk لكل قلاب
endmodule
